# Fritzing sketch Antifumo-WiFi (saved by Fritzing 0.9.3b)
breadboards: 1

parts:
  U1 = NodeMCU V1.0
  Componente1 = MQ-7 breakout

nets:
  VIN: U1.Vin, Componente1.VCC
  N1: U1.GND#33, Componente1.GND
  N2: U1.A0, Componente1.AO

notes:
  SIMORIA 1P2, SIstema de MOnitorización y RIego Automático., 1

custom parts:
  NodeMCU V1.0: ESP8266 based NodeMCU V1.0
  MQ-7 breakout: SKU: 101282
